# Fritzing sketch flip_clock_(ds1307) (saved by Fritzing 0.8.5b)
breadboards: 1

parts:
  S1 = Pushbutton [package="[THT]"]
  Часть2 = Real Time Clock Module - DS1307 RTC Breakout Board
  LED1 = LED - 5mm [color="Orange (620nm)" package="5 mm [THT]"]
  LED2 = LED - 5mm [color="Orange (620nm)" package="5 mm [THT]"]
  LED3 = LED - 5mm [color="Orange (620nm)" package="5 mm [THT]"]
  Часть3 = Arduino Nano (Rev3.0)
  R3 = Photocell (LDR) [package=THT]
  R4 = Resistor [tolerance=±5% resistance=220 package=THT]
  R6 = Resistor [tolerance=±5% resistance=4.7k package=THT]
  R7 = Resistor [tolerance=±5% resistance=4.7k package=THT]
  R11 = Resistor [tolerance=±5% resistance=220 package=THT]
  R12 = Resistor [tolerance=±5% resistance=220 package=THT]
  R13 = Resistor [tolerance=±5% resistance=220 package=THT]
  S2 = Pushbutton [package="[THT]"]

nets:
  N1: S1.Pin_1, S1.Pin_2, Часть3.D2, R7.Pin_0
  5V: S1.Pin_3, S1.Pin_4, Часть2.5V, Часть3.5V, R3.pin_0, S2.Pin_3, S2.Pin_4
  GND: Часть2.GND, LED1.cathode, LED2.cathode, LED3.cathode, Часть3.GND, R4.Pin_1, R6.Pin_1, R7.Pin_1
  N2: Часть2.SCL, Часть3.A5
  N3: Часть2.SDA, Часть3.A4
  N4: LED1.anode, R13.Pin_0
  N5: LED2.anode, R12.Pin_0
  N6: LED3.anode, R11.Pin_0
  N7: Часть3.D3, R11.Pin_1
  N8: Часть3.D4, R6.Pin_0, S2.Pin_1, S2.Pin_2
  N9: Часть3.D5, R12.Pin_1
  N10: Часть3.D6, R13.Pin_1
  N11: Часть3.A0, R3.pin_1, R4.Pin_0

notes:
  MODE
  PLUS
  alarm
  min
  hour
